# Fritzing sketch Untitled Sketch 2 (saved by Fritzing 1.0.4)
breadboards: 1

parts:
  A1 = Particle - Photon2  # not connected
  OLED_I2C1 = OLED 128x64 I2C Monochrome Display
  M1 = BMP280
  WATER_PUMP1 = water pump/motor  # not connected
  Relay1 = Relay - 6 pins [package="DIP (Dual Inline) [THT]"]
  Q1 = PNP-Transistor [package="TO92 [THT]"]
  R1 = Resistor [tolerance=±5% resistance=220 package="2512 [SMD]"]
  R2 = Resistor [tolerance=±5% resistance=2.2k package="2512 [SMD]"]
  SENS1 = SoilWatch 10

nets:
  N1: OLED_I2C1.SDA, M1.SDA
  N2: OLED_I2C1.SCK, M1.SCL
  VDD: OLED_I2C1.VDD, M1.VIN, SENS1.VCC
  GND: OLED_I2C1.GND, M1.GND, Q1.E, R2.Pin_0, SENS1.GND
  N3: Relay1.ON, R1.Pin_1
  N4: Q1.B, R2.Pin_1
  N5: Q1.C, R1.Pin_0

custom parts:
  Particle - Photon2: The Photon 2 is a microcontroller and Wi-Fi networking developed by particle. Features: 802.11a/b/g/n Wi-Fi, 2.4 GHz and 5 GHz Integrated PCB antenna Integrated U.FL connector for external antenna Integrated RF switch BLE 5 using same antenna as Wi-Fi Realtek RTL8721DM MCU ARM Cortex M33 CPU, 200 MHz 2048 KB (2 MB) user application maximum size 3072 KB (3 MB) of RAM available to user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
  BMP280: Temperature Humidity Barometric presure Sensor, I2C
  water pump/motor: WATER PUMP BY ARDUBLOCKTR
  Relay - 6 pins: A DIP stand-in part for whatever IC you want. With 6 pins on a 900mil dual inline package (DIP) footprint.
  SoilWatch 10: SoilWatch 10 - Capacitive soil moisture sensor
